// Digital circuit mult_soma.dig as structural Verilog
module mult_soma (
  input  A_0_B_0,
  input  A_1_B_0,
  input  A_0_B_1,
  input  A_2_B_0,
  input  A_1_B_1,
  input  A_3_B_0,
  input  A_2_B_1,
  input  A_3_B_1,
  output s_0,
  output s_1,
  output s_2,
  output s_3,
  output s_4,
  output s_5,
  output s_6,
  output s_7
);

  wire full_adder_1_p3, full_adder_2_p3, half_adder_1_p4;

  // half_adder half_adder_1: pin names not known; wires that end beside it: A_0_B_1, s_1, A_1_B_0, half_adder_1_p4
  // full_adder full_adder_1: pin names not known; wires that end beside it: A_2_B_0, half_adder_1_p4, full_adder_1_p3, A_1_B_1, s_2
  // full_adder full_adder_2: pin names not known; wires that end beside it: A_3_B_0, full_adder_1_p3, full_adder_2_p3, A_2_B_1, s_3
  // half_adder half_adder_2: pin names not known; wires that end beside it: A_3_B_1, s_4, full_adder_2_p3, s_5
  xnor xnor_1 (s_6, A_3_B_1, ~A_3_B_1);  // XNOr

  assign s_0 = A_0_B_0;
  assign s_7 = s_6;
endmodule
