// Digital circuit mult_soma2.dig as structural Verilog
module mult_soma2 (
  input  A_0_B_2,
  input  A_0_B_3,
  input  A_1_B_2,
  input  A_1_B_3,
  input  A_2_B_2,
  input  A_3_B_2,
  input  A_2_B_3,
  input  A_3_B_3,
  output s_0,
  output s_1,
  output s_2,
  output s_3,
  output s_4,
  output s_5,
  output s_6,
  output s_7
);

  wire full_adder_1_p3, full_adder_2_p3, half_adder_1_p4;

  xnor xnor_1 (s_0, A_0_B_2, ~A_0_B_2);  // XNOr
  // half_adder half_adder_1: pin names not known; wires that end beside it: A_1_B_2, s_3, A_0_B_3, half_adder_1_p4
  // full_adder full_adder_1: pin names not known; wires that end beside it: A_2_B_2, half_adder_1_p4, full_adder_1_p3, A_1_B_3, s_4
  // full_adder full_adder_2: pin names not known; wires that end beside it: A_3_B_2, full_adder_1_p3, full_adder_2_p3, A_2_B_3, s_5
  // half_adder half_adder_2: pin names not known; wires that end beside it: A_3_B_3, s_6, full_adder_2_p3, s_7

  assign s_1 = s_0;
  assign s_2 = A_0_B_2;
endmodule
