// Digital circuit mult_soma_final.dig as structural Verilog
module mult_soma_final (
  input  B_0,
  input  A_1,
  input  A_2,
  input  A_3,
  input  A_4,
  input  A_5,
  input  A_6,
  input  A_7,
  input  A_0,
  input  B_1,
  input  B_2,
  input  B_3,
  input  B_4,
  input  B_5,
  input  B_6,
  input  B_7,
  output s_0,
  output s_1,
  output s_2,
  output s_3,
  output s_4,
  output s_5,
  output s_6,
  output s_7
);

  wire full_adder_1_p3, full_adder_2_p3, full_adder_3_p3, full_adder_4_p3, full_adder_5_p3, full_adder_6_p3,
       full_adder_7_p3, half_adder_1_p4;

  // half_adder half_adder_1: pin names not known; wires that end beside it: B_0, s_0, A_0, half_adder_1_p4
  // full_adder full_adder_1: pin names not known; wires that end beside it: A_1, half_adder_1_p4, full_adder_1_p3, B_1, s_1
  // full_adder full_adder_2: pin names not known; wires that end beside it: A_2, full_adder_1_p3, full_adder_2_p3, B_2, s_2
  // full_adder full_adder_3: pin names not known; wires that end beside it: A_3, full_adder_2_p3, full_adder_3_p3, B_3, s_3
  // full_adder full_adder_4: pin names not known; wires that end beside it: A_4, full_adder_3_p3, full_adder_4_p3, B_4, s_4
  // full_adder full_adder_5: pin names not known; wires that end beside it: A_5, full_adder_4_p3, full_adder_5_p3, B_5, s_5
  // full_adder full_adder_6: pin names not known; wires that end beside it: A_6, full_adder_5_p3, full_adder_6_p3, B_6, s_6
  // full_adder full_adder_7: pin names not known; wires that end beside it: A_7, full_adder_6_p3, full_adder_7_p3, B_7, s_7
  LED led_1 (.in(full_adder_7_p3));
endmodule
