// Digital circuit multiplex.dig as structural Verilog
module multiplex (
  input  O_0,
  input  O_1,
  input  O_2,
  input  O_3,
  input  S_0,
  input  S_1,
  output Z
);

  wire and_1_out, and_2_out, and_3_out, and_4_out, not_1_out, not_2_out;

  not not_1 (not_1_out, S_1);
  and and_1 (and_1_out, O_0, not_1_out, not_2_out);
  and and_2 (and_2_out, O_1, not_1_out, S_0);
  and and_3 (and_3_out, O_2, S_1, not_2_out);
  and and_4 (and_4_out, O_3, S_1, S_0);
  not not_2 (not_2_out, S_0);
  or or_1 (Z, and_1_out, and_2_out, and_3_out, and_4_out);
endmodule
