// Digital circuit multiplicador.dig as structural Verilog
module multiplicador (
  input  A_0,
  input  A_1,
  input  A_2,
  input  A_3,
  input  B_0,
  input  B_1,
  input  B_2,
  input  B_3,
  output s_0,
  output s_1,
  output s_2,
  output s_3,
  output s_4,
  output s_5,
  output s_6,
  output s_7
);

  wire and_1_out, and_2_out, and_3_out, and_4_out, and_5_out, and_6_out, and_7_out, and_8_out, and_9_out,
       and_10_out, and_11_out, and_12_out, and_13_out, and_14_out, and_15_out, and_16_out, mult_soma2_1_s_0,
       mult_soma2_1_s_1, mult_soma2_1_s_2, mult_soma2_1_s_3, mult_soma2_1_s_4, mult_soma2_1_s_5,
       mult_soma2_1_s_6, mult_soma2_1_s_7, mult_soma_1_s_0, mult_soma_1_s_1, mult_soma_1_s_2,
       mult_soma_1_s_3, mult_soma_1_s_4, mult_soma_1_s_5, mult_soma_1_s_6, mult_soma_1_s_7;

  and and_1 (and_1_out, A_3, B_3);
  and and_2 (and_2_out, A_2, B_3);
  and and_3 (and_3_out, A_3, B_2);
  and and_4 (and_4_out, A_2, B_2);
  and and_5 (and_5_out, A_1, B_3);
  and and_6 (and_6_out, A_1, B_2);
  and and_7 (and_7_out, A_0, B_3);
  mult_soma2 mult_soma2_1 (
    .A_0_B_2(and_8_out), .A_0_B_3(and_7_out), .A_1_B_2(and_6_out), .A_1_B_3(and_5_out), .A_2_B_2(and_4_out),
    .A_3_B_2(and_3_out), .A_2_B_3(and_2_out), .A_3_B_3(and_1_out), .s_0(mult_soma2_1_s_0),
    .s_1(mult_soma2_1_s_1), .s_2(mult_soma2_1_s_2), .s_3(mult_soma2_1_s_3), .s_4(mult_soma2_1_s_4),
    .s_5(mult_soma2_1_s_5), .s_6(mult_soma2_1_s_6), .s_7(mult_soma2_1_s_7));
  and and_8 (and_8_out, A_0, B_2);
  and and_9 (and_9_out, A_3, B_1);
  and and_10 (and_10_out, A_2, B_1);
  and and_11 (and_11_out, A_3, B_0);
  and and_12 (and_12_out, A_1, B_1);
  and and_13 (and_13_out, A_2, B_0);
  and and_14 (and_14_out, A_0, B_1);
  and and_15 (and_15_out, A_1, B_0);
  mult_soma mult_soma_1 (
    .A_0_B_0(and_16_out), .A_1_B_0(and_15_out), .A_0_B_1(and_14_out), .A_2_B_0(and_13_out),
    .A_1_B_1(and_12_out), .A_3_B_0(and_11_out), .A_2_B_1(and_10_out), .A_3_B_1(and_9_out),
    .s_0(mult_soma_1_s_0), .s_1(mult_soma_1_s_1), .s_2(mult_soma_1_s_2), .s_3(mult_soma_1_s_3),
    .s_4(mult_soma_1_s_4), .s_5(mult_soma_1_s_5), .s_6(mult_soma_1_s_6), .s_7(mult_soma_1_s_7));
  and and_16 (and_16_out, A_0, B_0);
  mult_soma_final mult_soma_final_1 (
    .B_0(mult_soma2_1_s_0), .A_1(mult_soma_1_s_1), .A_2(mult_soma_1_s_2), .A_3(mult_soma_1_s_3),
    .A_4(mult_soma_1_s_4), .A_5(mult_soma_1_s_5), .A_6(mult_soma_1_s_6), .A_7(mult_soma_1_s_7),
    .A_0(mult_soma_1_s_0), .B_1(mult_soma2_1_s_1), .B_2(mult_soma2_1_s_2), .B_3(mult_soma2_1_s_3),
    .B_4(mult_soma2_1_s_4), .B_5(mult_soma2_1_s_5), .B_6(mult_soma2_1_s_6), .B_7(mult_soma2_1_s_7),
    .s_0(s_0), .s_1(s_1), .s_2(s_2), .s_3(s_3), .s_4(s_4), .s_5(s_5), .s_6(s_6), .s_7(s_7));
endmodule
